// Logisim project MIPS-like.circ as structural Verilog: 5 circuits, main circuit main
module main (
);

  wire ALUSrc, Branch, clear, clock, Jump, MemRead, MemToReg, MemWrite, RegDst, RegWrite, tunnel;
  wire [1:0] ALUOp;
  wire [2:0] OPCode, ULA_C;
  wire [3:0] multiplexer_1_out;
  wire [4:0] rom_1_data;
  wire [7:0] PC, PCSum;
  wire [23:0] Address;
  wire [31:0] bit_extender_1_out, multiplexer_2_out, R1, R2, ULAOut;

  Clock clock_1 (.out(clock));
  Button button_1 (.out(clear));
  UC uc_1 (
    .Opcode(OPCode), .RegDst(RegDst), .RegWrite(RegWrite), .ALUSrc(ALUSrc), .MemWrite(MemWrite),
    .MemRead(MemRead), .MemToReg(MemToReg), .Branch(Branch), .Jump(Jump), .ALUOp(ALUOp));
  RAM #(.dataWidth(32), .Select("low")) ram_1 ();  // open: addr, data, sel, clk, ld, clr
  ROM #(.dataWidth(32), .Select("high")) rom_1 (.addr(PC), .data({OPCode, Address, rom_1_data}));
  Controle_ULA controle_ula_1 (.Func(Address[6:4]), .ALUop(ALUOp), .ALUCtrl(ULA_C));
  Register #(.Select("low")) register_1 (.D(PCSum), .Q(PC), .clk(clock), .clr(clear));  // open: en
  Adder adder_1 (.a(8'h4), .b(PC), .out(PCSum));  // open: cin, cout
  Multiplexer #(.width(4), .enable("false")) multiplexer_1 (
    .in0(Address[23:20]), .in1(Address[15:12]), .out(multiplexer_1_out), .sel(RegDst));
  assign bit_extender_1_out = {{16{1'b0}}, Address[15:0]};  // Bit_Extender bit_extender_1
  Multiplexer #(.width(32), .enable("false")) multiplexer_2 (
    .in0(R2), .in1(bit_extender_1_out), .out(multiplexer_2_out), .sel(ALUSrc));
  Banco_de_Registradores banco_de_registradores_1 (
    .Read_register_1(Address[23:20]), .Read_register_2(Address[19:16]), .Write_register(multiplexer_1_out),
    .CLOCK(clock), .CLEAR(clear), .RW(RegWrite), .Read_data_1(R1), .Read_data_2(R2));  // open: Write_data
  ULA ula_1 (
    .Data_0(R1), .Data_1(multiplexer_2_out), .Shamt(Address[11:7]), .Func(ULA_C), .out_5(tunnel),
    .Resultado(ULAOut));

  // Other names for the same wires on the sheet: Imm[15:0] = Address[15:0]; Func[2:0] = Address[6:4];
  //   Shamt[4:0] = Address[11:7]; RD[3:0] = Address[15:12]; RT[3:0] = Address[19:16]; RS[3:0] = Address[23:20]

  // Notes on the sheet:
  //   CLOCK E CLEAR
  //   CONTROL UNIT
  //   DATA MEMORY
  //   INSTRUCTION MEMORY
  //   ULA CONTROL
  //   PROGRAM COUNTER
  //   BANCO DE REGISTRADORES
  //   ULA
endmodule

module Banco_de_Registradores (
  input  [3:0] Read_register_1,
  input  [3:0] Read_register_2,
  input  [3:0] Write_register,
  input  [31:0] Write_data,
  input  CLOCK,
  input  CLEAR,
  input  RW,
  output [31:0] Read_data_1,
  output [31:0] Read_data_2
);

  wire WE0, WE1, WE2, WE3, WE4, WE5, WE6, WE7, WE9, WE10, WE11, WE12, WE13, WE14, WE15, WE16;
  wire [31:0] Reg0, Reg1, Reg2, Reg3, Reg4, Reg5, Reg6, Reg7, Reg8, Reg9, Reg10, Reg11, Reg12, Reg13, Reg14,
       Reg15;

  Demultiplexer #(.select(4), .enable("false")) demultiplexer_1 (
    .out0(WE0), .out1(WE1), .out2(WE2), .out3(WE3), .out4(WE4), .out5(WE5), .out6(WE6), .out7(WE7),
    .out8(WE9), .out9(WE10), .out10(WE11), .out11(WE12), .out12(WE13), .out13(WE14), .out14(WE15),
    .out15(WE16), .in(RW), .sel(Write_register));
  Multiplexer #(.select(4), .width(32), .enable("false")) multiplexer_1 (
    .in0(Reg0), .in1(Reg1), .in2(Reg2), .in3(Reg3), .in4(Reg4), .in5(Reg5), .in6(Reg6), .in7(Reg7),
    .in8(Reg8), .in9(Reg9), .in10(Reg10), .in11(Reg11), .in12(Reg12), .in13(Reg13), .in14(Reg14),
    .in15(Reg15), .out(Read_data_1), .sel(Read_register_1));
  Register #(.width(32), .Select("low")) register_1 (.D(Write_data), .en(WE0), .Q(Reg0), .clk(CLOCK), .clr(CLEAR));
  Register #(.width(32), .Select("low")) register_2 (.D(Write_data), .en(WE1), .Q(Reg1), .clk(CLOCK), .clr(CLEAR));
  Register #(.width(32), .Select("low")) register_3 (.D(Write_data), .en(WE2), .Q(Reg2), .clk(CLOCK), .clr(CLEAR));
  Register #(.width(32), .Select("low")) register_4 (.D(Write_data), .en(WE3), .Q(Reg3), .clk(CLOCK), .clr(CLEAR));
  Register #(.width(32), .Select("low")) register_5 (.D(Write_data), .en(WE4), .Q(Reg4), .clk(CLOCK), .clr(CLEAR));
  Register #(.width(32), .Select("low")) register_6 (.D(Write_data), .en(WE5), .Q(Reg5), .clk(CLOCK), .clr(CLEAR));
  Register #(.width(32), .Select("low")) register_7 (.D(Write_data), .en(WE6), .Q(Reg6), .clk(CLOCK), .clr(CLEAR));
  Register #(.width(32), .Select("low")) register_8 (.D(Write_data), .en(WE7), .Q(Reg7), .clk(CLOCK), .clr(CLEAR));
  Register #(.width(32), .Select("low")) register_9 (.D(Write_data), .en(WE9), .Q(Reg8), .clk(CLOCK), .clr(CLEAR));
  Register #(.width(32), .Select("low")) register_10 (.D(Write_data), .en(WE10), .Q(Reg9), .clk(CLOCK), .clr(CLEAR));
  Register #(.width(32), .Select("low")) register_11 (.D(Write_data), .en(WE11), .Q(Reg10), .clk(CLOCK), .clr(CLEAR));
  Register #(.width(32), .Select("low")) register_12 (.D(Write_data), .en(WE12), .Q(Reg11), .clk(CLOCK), .clr(CLEAR));
  Register #(.width(32), .Select("low")) register_13 (.D(Write_data), .en(WE13), .Q(Reg12), .clk(CLOCK), .clr(CLEAR));
  Register #(.width(32), .Select("low")) register_14 (.D(Write_data), .en(WE14), .Q(Reg13), .clk(CLOCK), .clr(CLEAR));
  Register #(.width(32), .Select("low")) register_15 (.D(Write_data), .en(WE15), .Q(Reg14), .clk(CLOCK), .clr(CLEAR));
  Register #(.width(32), .Select("low")) register_16 (.D(Write_data), .en(WE16), .Q(Reg15), .clk(CLOCK), .clr(CLEAR));
  Multiplexer #(.select(4), .width(32), .enable("false")) multiplexer_2 (
    .in0(Reg0), .in1(Reg1), .in2(Reg2), .in3(Reg3), .in4(Reg4), .in5(Reg5), .in6(Reg6), .in7(Reg7),
    .in8(Reg8), .in9(Reg9), .in10(Reg10), .in11(Reg11), .in12(Reg12), .in13(Reg13), .in14(Reg14),
    .in15(Reg15), .out(Read_data_2), .sel(Read_register_2));

  // Other names for the same wires on the sheet: CLK = CLOCK; Data[31:0] = Write_data; Read_1[3:0] = Read_register_1;
  //   Read_2[3:0] = Read_register_2; WR[3:0] = Write_register

  // Notes on the sheet:
  //   ENTRADAS
  //   SELEÇÃO DE REGISTRADOR
  //   SAÍDA REGISTRADOR 1
  //   REGISTRADORES
  //   SAÍDA REGISTRADOR 2
endmodule

module ULA (
  input  [31:0] Data_0,
  input  [31:0] Data_1,
  input  [4:0] Shamt,
  input  [2:0] Func,
  output out_5,
  output [31:0] Resultado
);

  wire Igualdade, tunnel;
  wire [31:0] AComp, ADiv, AMult, ANeg, ANegSaida, AShiftDir, AShiftEsq, ASoma, ASub, BComp, BDiv, BMult,
       BSoma, BSub, CompSaida, DivSaida, MultSaida, ShiftDirSaida, ShiftEsqSaida, SomaSaida, SubSaida;

  Demultiplexer #(.select(3), .width(32), .enable("false")) demultiplexer_1 (
    .out0(ASoma), .out1(ASub), .out2(AMult), .out3(ADiv), .out4(ANeg), .out5(AComp), .out6(AShiftEsq),
    .out7(AShiftDir), .in(Data_0), .sel(Func));
  Demultiplexer #(.select(3), .width(32), .enable("false")) demultiplexer_2 (
    .out0(BSoma), .out1(BSub), .out2(BMult), .out3(BDiv), .out5(BComp), .in(Data_1), .sel(Func));  // open: out4, out6, out7
  Adder #(.width(32)) adder_1 (.a(ASoma), .b(BSoma), .out(SomaSaida));  // open: cin, cout
  Subtractor #(.width(32)) subtractor_1 (.a(ASub), .b(BSub), .out(SubSaida));  // open: bin, bout
  Multiplier #(.width(32)) multiplier_1 (.a(AMult), .b(BMult), .out(MultSaida));  // open: cin, cout
  Divider #(.width(32)) divider_1 (.a(ADiv), .b(BDiv), .out(DivSaida));  // open: upper, rem
  Comparator #(.width(32)) comparator_1 (.a(AComp), .b(BComp), .gt(tunnel), .eq(Igualdade));  // open: lt
  Negator #(.width(32)) negator_1 (.in(ANeg), .out(ANegSaida));
  Shifter #(.width(32)) shifter_1 (.in(AShiftEsq), .\dist (Shamt), .out(ShiftEsqSaida));
  Shifter #(.width(32), .shift("lr")) shifter_2 (.in(AShiftDir), .\dist (Shamt), .out(ShiftDirSaida));
  assign CompSaida = {{31{1'b0}}, Igualdade};  // Bit_Extender bit_extender_1
  or or_1 (out_5, tunnel, Igualdade);
  Multiplexer #(.select(3), .width(32), .enable("false")) multiplexer_1 (
    .in0(SomaSaida), .in1(SubSaida), .in2(MultSaida), .in3(DivSaida), .in4(ANegSaida), .in5(CompSaida),
    .in6(ShiftEsqSaida), .in7(ShiftDirSaida), .out(Resultado), .sel(Func));

  // Other names for the same wires on the sheet: A[31:0] = Data_0; B[31:0] = Data_1

  // Notes on the sheet:
  //   ENTRADAS
endmodule

module UC (
  input  [2:0] Opcode,
  output RegDst,
  output RegWrite,
  output ALUSrc,
  output MemWrite,
  output MemRead,
  output MemToReg,
  output Branch,
  output Jump,
  output [1:0] ALUOp
);

  wire and_1_out, and_4_out, and_5_out, and_8_out, and_9_out, nor_2_out;

  nor nor_1 (RegDst, Opcode[0], Opcode[1], Opcode[2]);
  nor nor_2 (nor_2_out, Opcode[1], Opcode[2]);
  and and_1 (and_1_out, ~Opcode[0], ~Opcode[1], Opcode[2]);  // AND_Gate
  ExactlyOne xor_1 (.out(ALUSrc), .in0(Opcode[0]), .in1(Opcode[1]), .in2(Opcode[2]));
  and and_2 (MemWrite, ~Opcode[0], Opcode[1], ~Opcode[2]);  // AND_Gate
  and and_3 (MemRead, Opcode[0], ~Opcode[1], ~Opcode[2]);  // AND_Gate
  and and_4 (and_4_out, ~Opcode[0], ~Opcode[1], ~Opcode[2]);  // AND_Gate
  and and_5 (and_5_out, ~Opcode[0], ~Opcode[1], Opcode[2]);  // AND_Gate
  and and_6 (Branch, Opcode[0], Opcode[1], ~Opcode[2]);  // AND_Gate
  and and_7 (Jump, Opcode[0], Opcode[1], Opcode[2]);
  and and_8 (and_8_out, Opcode[0], Opcode[1], ~Opcode[2]);  // AND_Gate
  and and_9 (and_9_out, ~Opcode[0], ~Opcode[1], Opcode[2]);  // AND_Gate
  and and_10 (ALUOp[1], ~Opcode[0], ~Opcode[1]);  // AND_Gate
  or or_1 (RegWrite, nor_2_out, and_1_out);
  or or_2 (MemToReg, and_4_out, and_5_out);
  or or_3 (ALUOp[0], and_8_out, and_9_out);
endmodule

module Controle_ULA (
  input  [2:0] Func,
  input  [1:0] ALUop,
  output [2:0] ALUCtrl
);

  Multiplexer #(.select(2), .width(3), .enable("false")) multiplexer_1 (
    .in0(3'b000), .in1(3'b101), .in2(Func), .in3(3'b000), .out(ALUCtrl), .sel(ALUop));
endmodule
